# Fritzing sketch ASL_glove (saved by Fritzing 0.9.2b)
breadboards: 2

parts:
  Part1 = Arduino Nano (Rev3.0) (ICSP)
  Part2 = Arduino Nano (Rev3.0) (ICSP)
  GY1 = MPU-6050 Board GY-521 [form="♀ (female)" package=THT]  # not connected
  Part3 = Logic Level Converter
  R1 = Basic Flex Resistor
  R2 = Basic Flex Resistor
  R3 = Basic Flex Resistor
  R4 = Basic Flex Resistor
  R5 = Basic Flex Resistor
  R7 = Resistor [tolerance=±5% resistance=33k package=THT]
  R8 = Resistor [tolerance=±5% resistance=33k package=THT]
  R9 = Resistor [tolerance=±5% resistance=33k package=THT]
  R10 = Resistor [tolerance=±5% resistance=33k package=THT]
  R11 = Resistor [tolerance=±5% resistance=33k package=THT]
  LED2 = smd LED [color="Red (633nm)" package="0805 [SMD]"]
  SD_card_module1 = SD Card Module
  U1 = LCD-16X2 [package=lcd-16x2]
  S1 = Pushbutton [package="[SMD]"]
  R12 = Resistor [tolerance=±5% resistance=10k package=THT]
  C1 = Ceramic Capacitor [capacitance="100 nF" package="0603 [SMD, multilayer]"]
  R13 = Resistor [tolerance=±5% resistance=220 package=THT]
  LED3 = LED - 5mm [color="Red (633nm)" package="5 mm [THT]"]

nets:
  N1: Part1.D1/TX, Part3.TX2_HV
  N2: Part1.D0/RX, Part3.RX2_HV
  GND: Part1.GND, Part2.GND, Part3.GND, R7.Pin_1, R8.Pin_1, R9.Pin_1, R10.Pin_1, R11.Pin_1, LED2.cathode, SD_card_module1.GND, U1.VSS, U1.R_W, U1.K, S1.Pin_3, S1.Pin_4, C1.0, LED3.cathode
  N3: Part1.D2, U1.DB7
  N4: Part1.D3, U1.DB6
  N5: Part1.D4, SD_card_module1.CS
  N6: Part1.D5, U1.DB4
  N7: Part1.D6, Part3.TX_HV, LED3.anode
  N8: Part1.D7, U1.DB5
  N9: Part1.D9, U1.E
  N10: Part1.D10, U1.RS
  N11: Part1.D11/MOSI, SD_card_module1.MOSI
  N12: Part1.D12/MISO, SD_card_module1.MISO
  5V: Part1.5V, Part2.VIN, Part3.HV, SD_card_module1.+5, U1.VDD, R12.Pin_1, R13.Pin_1
  N13: Part1.A5, S1.Pin_1, S1.Pin_2, R12.Pin_0, C1.1
  N14: Part1.D13/SCK, SD_card_module1.SCK
  N15: Part2.D1/TX, Part3.RX2_LV
  N16: Part2.D0/RX, Part3.TX2_LV
  N17: Part2.D2, Part3.TX_LV
  N18: Part2.A7, R5.pin_1, R10.Pin_0
  N19: Part2.A3, R3.pin_1, R11.Pin_0
  N20: Part2.A2, R2.pin_1, R7.Pin_0
  N21: Part2.A1, R1.pin_1, R8.Pin_0
  N22: Part2.A0, R4.pin_1, R9.Pin_0
  N23: Part2.3V3, Part3.LV, R1.Pin_2, R2.Pin_2, R3.Pin_2, R4.Pin_2, R5.Pin_2
  N24: Part2.D13/SCK, LED2.anode
  N25: U1.A, R13.Pin_0

custom parts:
  MPU-6050 Board GY-521: Acelerometro y Giroscopio MPU-6050 Board GY-521
  SD Card Module: SD Card Module Slot Socket Reader For Arduino ARM MCU
